# Fritzing sketch ServoBlume_MK1 (saved by Fritzing 0.9.10b)
breadboards: 1

parts:
  Bauteil1 = Arduino Uno (Rev3) - ICSP
  TM1638_-_Led_Button_Module1 = IC, DIP package, 10 pins [chip_label=TM1638]
  J1 = Basic Servo
  BUTTON1 = Arcade Button (blue)
  C1 = Electrolytic Capacitor [capacitance=100µF voltage=35V package="100 mil [THT, electrolytic]"]

nets:
  5V: Bauteil1.5V, TM1638_-_Led_Button_Module1.pin1, J1.vcc, C1.+
  GND: Bauteil1.GND, TM1638_-_Led_Button_Module1.pin2, J1.gnd, BUTTON1.no_name_yet#2, C1.-
  N1: Bauteil1.D3_PWM, TM1638_-_Led_Button_Module1.pin3
  N2: Bauteil1.D4, TM1638_-_Led_Button_Module1.pin4
  N3: Bauteil1.D5_PWM, TM1638_-_Led_Button_Module1.pin5
  N4: Bauteil1.D6_PWM, J1.pulse
  N5: Bauteil1.D7, BUTTON1.no_name_yet#1

custom parts:
  Arcade Button (blue): Adafruit Arcade Button (blue)
